# Fritzing sketch nikon_d3000_intervalometer_breadboard (saved by Fritzing 0.9.3b)
breadboards: 1

parts:
  OLED = OLED 0.96" 128x64 I2C SSD1306
  D1 = LTE-302 [package=lte-302]
  S1 = Momentary Switch [part_number=Select package=ksa_sealed_tac_switch]
  S2 = Momentary Switch [part_number=Up package=ksa_sealed_tac_switch]
  S3 = Momentary Switch [part_number=Down package=ksa_sealed_tac_switch]
  Arduino_Nano = Arduino Nano (Rev3.0) (ICSP)
  R2 = Resistor [tolerance=±5% resistance=10k package="0603 [SMD]"]
  R3 = Resistor [tolerance=±5% resistance=10k package="0603 [SMD]"]
  R4 = Resistor [tolerance=±5% resistance=10k package="0603 [SMD]"]
  R5 = Resistor [tolerance=±5% resistance=220 package=THT]
  J1 = Piezo Speaker [part_number=Buzzer]

nets:
  VCC: OLED.VCC, S1.2, S2.2, S3.2, Arduino_Nano.5V
  GND: OLED.GND, D1.C, Arduino_Nano.GND, R2.Pin_0, R3.Pin_0, R4.Pin_0, J1.pin1
  N1: OLED.SCL, Arduino_Nano.A5
  N2: OLED.SCA, Arduino_Nano.A4
  N3: D1.A, R5.Pin_1
  N4: S1.3, Arduino_Nano.D5, R4.Pin_1
  N5: S2.3, Arduino_Nano.D2, R2.Pin_1
  N6: S3.3, Arduino_Nano.D3, R3.Pin_1
  N7: Arduino_Nano.D6, R5.Pin_0
  N8: Arduino_Nano.D7, J1.pin2
